# Fritzing sketch SimonPCB (saved by Fritzing 0.8.3b)
circuit board: 6.18822cm x 5.9842cm
breadboards: 1

parts:
  GPIO = Adafruit Pi Cobbler
  S1 = Pushbutton [package="[THT]"]
  LED1 = LED - 5mm [color="Red (633nm)" package="5 mm [THT]"]
  R2 = Resistor [tolerance=±5% resistance=330 package=THT]
  R8 = Resistor [tolerance=±5% resistance=10k package=THT]
  S2 = Pushbutton [package="[THT]"]
  LED2 = LED - 5mm [color="Green (555nm)" package="5 mm [THT]"]
  R9 = Resistor [tolerance=±5% resistance=330 package=THT]
  R10 = Resistor [tolerance=±5% resistance=10k package=THT]
  S3 = Pushbutton [package="[THT]"]
  LED3 = LED - 5mm [color="Yellow (585nm)" package="5 mm [THT]"]
  R11 = Resistor [tolerance=±5% resistance=330 package=THT]
  R12 = Resistor [tolerance=±5% resistance=10k package=THT]
  S4 = Pushbutton [package="[THT]"]
  LED4 = LED - 5mm [color="Blue (430nm)" package="5 mm [THT]"]
  R13 = Resistor [tolerance=±5% resistance=330 package=THT]
  R14 = Resistor [tolerance=±5% resistance=10k package=THT]

nets (from the pcb view):
  N1: GPIO.#21, R9.Pin_0
  N2: GPIO.PIN14, S2.Pin_1, S2.Pin_2, LED2.cathode, S3.Pin_1, S3.Pin_2, LED3.cathode
  N3: GPIO.#22, R11.Pin_0
  N4: GPIO.#23, R13.Pin_0
  N5: GPIO.PIN19, R8.Pin_0, R10.Pin_0, R12.Pin_0, R14.Pin_0
  N6: GPIO.#24, R2.Pin_0
  N7: GPIO.PIN20, GPIO.#25, S1.Pin_1, S1.Pin_2, LED1.cathode, S2.Pin_3, S2.Pin_4, R10.Pin_1, S4.Pin_1, S4.Pin_2, LED4.cathode
  N8: GPIO.MISO, S4.Pin_3, S4.Pin_4, R14.Pin_1
  N9: GPIO.SCLK, S1.Pin_3, S1.Pin_4, R8.Pin_1
  N10: GPIO.CE0, S3.Pin_3, S3.Pin_4, R12.Pin_1
  N11: LED1.anode, R2.Pin_1
  N12: LED2.anode, R9.Pin_1
  N13: LED3.anode, R11.Pin_1
  N14: LED4.anode, R13.Pin_1

custom parts:
  Adafruit Pi Cobbler: Adafruit Pi Cobbler GPIO Breakout for Raspberry Pi
